# Fritzing sketch Fritzing (saved by Fritzing 0.9.4)
perfboards: 1

parts:
  Bauteil1 = Arduino Uno (Rev3) - ICSP
  Bauteil2 = Bluetooth HC-05 Macho
  LED1 = smd LED [color="Red (633nm)" package="1206 [SMD]"]
  LED2 = smd LED [color="Blue (430nm)" package="1206 [SMD]"]
  LED3 = smd LED [color="Green (555nm)" package="1206 [SMD]"]
  R4 = Resistor [tolerance=±5% resistance=220 package=THT]
  R5 = Resistor [tolerance=±5% resistance=220 package=THT]
  R6 = Resistor [tolerance=±5% resistance=220 package=THT]
  Chirp!_Soil_Moisture_Sensor1 = Chirp! Soil Moisture Sensor v2.7.3
  Bauteil3 = Jtron 1 Channel Optoisolated Relay Module [package=relay]
  VCC1 = Battery block 9V
  U1 = Transformer [package=transformer]
  Chirp!_Soil_Moisture_Sensor2 = Chirp! Soil Moisture Sensor v2.7.3

nets:
  N1: Bauteil1.A0, Chirp!_Soil_Moisture_Sensor1.pin_3
  N2: Bauteil1.A1, Chirp!_Soil_Moisture_Sensor2.pin_3
  N3: Bauteil1.D11_PWM/MOSI, Bauteil2.RXD
  N4: Bauteil1.D12/MISO, Bauteil2.TXD
  GND: Bauteil1.GND, Bauteil2.GND, R4.Pin_0, Chirp!_Soil_Moisture_Sensor1.pin_5, Bauteil3.GND, Chirp!_Soil_Moisture_Sensor2.pin_5
  N5: Bauteil1.D2, Bauteil3.IN1
  N6: Bauteil1.D6_PWM, LED3.anode
  N7: Bauteil1.3V3, Chirp!_Soil_Moisture_Sensor1.Pin_1, Chirp!_Soil_Moisture_Sensor2.Pin_1
  VCC: Bauteil1.5V, Bauteil2.VCC, Bauteil3.VCC
  N8: LED1.cathode, R4.Pin_1
  N9: LED2.cathode, R6.Pin_1
  N10: LED3.cathode, R5.Pin_1
  N11: Bauteil3.NO, VCC1.-
  N12: Bauteil3.MAIN, U1.2
  N13: VCC1.+, U1.3

notes:
  Transformator (Looks different)
  Relay
  Upper Moisture Sensor
  Bluetooth Module
  Lower Moisture Sensor
